// Logisim project OFFLINE_1.circ as structural Verilog: 3 circuits, main circuit 1 Bit ALU
module _1_Bit_ALU (
  input  Cin,
  input  CS2,
  input  CS1,
  input  CS0,
  input  A,
  input  B,
  output \output ,
  output Cout
);

  wire and_1_out, and_2_out, and_3_out, and_4_out, and_5_out, not_1_out, not_2_out, not_3_out, or_1_out,
       or_2_out;

  not not_1 (not_1_out, B);
  not not_2 (not_2_out, CS2);
  and and_1 (and_1_out, B, not_2_out, CS1);
  and and_2 (and_2_out, CS2, not_1_out);
  not not_3 (not_3_out, CS1);
  and and_3 (and_3_out, CS1, CS2);
  and and_4 (and_4_out, not_2_out, not_3_out);
  or or_1 (or_1_out, A, and_1_out);
  and and_5 (and_5_out, not_3_out, Cin);
  or or_2 (or_2_out, and_4_out, and_3_out, and_2_out);
  Adder #(.width(1)) adder_1 (.a(or_1_out), .b(or_2_out), .out(\output ), .cin(and_5_out), .cout(Cout));
endmodule

module _4_bit_ALU (
  input  [2:0] in_1,
  input  [3:0] A,
  input  [3:0] B,
  output ZERO,
  output SIGN,
  output OVERFLOW,
  output CARRY,
  output [3:0] OUTPUT
);

  wire n1_bit_alu_1_cout, n1_bit_alu_2_cout, n1_bit_alu_3_cout, n1_bit_alu_4_cout;

  _1_Bit_ALU u_1_bit_alu_1 (
    .CS2(in_1[2]), .CS1(in_1[1]), .A(A[0]), .B(B[0]), .CS0(in_1[0]), .\output (OUTPUT[0]),
    .Cout(n1_bit_alu_1_cout), .Cin(in_1[0]));
  _1_Bit_ALU u_1_bit_alu_2 (
    .CS2(in_1[2]), .CS1(in_1[1]), .A(A[1]), .B(B[1]), .CS0(in_1[0]), .\output (OUTPUT[1]),
    .Cout(n1_bit_alu_2_cout), .Cin(n1_bit_alu_1_cout));
  _1_Bit_ALU u_1_bit_alu_3 (
    .CS2(in_1[2]), .CS1(in_1[1]), .A(A[2]), .B(B[2]), .CS0(in_1[0]), .\output (OUTPUT[2]),
    .Cout(n1_bit_alu_3_cout), .Cin(n1_bit_alu_2_cout));
  _1_Bit_ALU u_1_bit_alu_4 (
    .CS2(in_1[2]), .CS1(in_1[1]), .A(A[3]), .B(B[3]), .CS0(in_1[0]), .\output (OUTPUT[3]),
    .Cout(n1_bit_alu_4_cout), .Cin(n1_bit_alu_3_cout));
  Flag_Register flag_register_1 (
    .OUTPUT(OUTPUT), .C4(n1_bit_alu_3_cout), .C5(n1_bit_alu_4_cout), .ZERO(ZERO), .SIGN(SIGN),
    .OVERFLOW(OVERFLOW), .CARRY(CARRY), .Selection(in_1));
endmodule

module Flag_Register (
  input  [2:0] Selection,
  input  [3:0] OUTPUT,
  input  C4,
  input  C5,
  output ZERO,
  output SIGN,
  output OVERFLOW,
  output CARRY
);

  wire and_1_out, not_1_out, not_2_out, xor_1_out;

  not not_1 (not_1_out, Selection[2]);
  and and_1 (and_1_out, Selection[1], not_1_out);
  not not_2 (not_2_out, and_1_out);
  nor nor_1 (ZERO, OUTPUT[0], OUTPUT[1], OUTPUT[2], OUTPUT[3]);
  xor xor_1 (xor_1_out, C4, C5);
  and and_2 (OVERFLOW, not_2_out, xor_1_out);
  and and_3 (CARRY, not_2_out, C5);

  assign SIGN = OUTPUT[3];
endmodule
