// Logisim project Purbasha_Given.circ as structural Verilog: 2 circuits, main circuit 1 Bit ALU
module _1_Bit_ALU (
  input  Cin,
  input  CS2,
  input  CS1,
  input  CS0,
  input  A,
  input  B,
  output \output ,
  output Cout
);

  wire and_1_out, and_2_out, and_3_out, and_4_out, and_5_out, not_1_out, not_2_out, not_3_out, or_1_out,
       or_2_out;

  not not_1 (not_1_out, B);
  not not_2 (not_2_out, CS2);
  and and_1 (and_1_out, B, not_2_out, CS1);
  and and_2 (and_2_out, CS2, not_1_out);
  not not_3 (not_3_out, CS1);
  and and_3 (and_3_out, CS1, CS2);
  and and_4 (and_4_out, not_2_out, not_3_out);
  or or_1 (or_1_out, A, and_1_out);
  and and_5 (and_5_out, not_3_out, Cin);
  or or_2 (or_2_out, and_4_out, and_3_out, and_2_out);
  Adder #(.width(1)) adder_1 (.a(or_1_out), .b(or_2_out), .out(\output ), .cin(and_5_out), .cout(Cout));
endmodule

module _4_bit_ALU (
  input  [2:0] in_1,
  input  [3:0] A,
  input  [3:0] B,
  output ZERO,
  output SIGN,
  output [3:0] out_6,
  output OVERFLOW,
  output CARRY
);

  wire n1_bit_alu_1_cout, n1_bit_alu_2_cout, n1_bit_alu_3_cout;

  _1_Bit_ALU u_1_bit_alu_1 (
    .CS2(in_1[2]), .CS1(in_1[1]), .A(A[0]), .B(B[0]), .CS0(in_1[0]), .\output (out_6[0]),
    .Cout(n1_bit_alu_1_cout), .Cin(in_1[0]));
  _1_Bit_ALU u_1_bit_alu_2 (
    .CS2(in_1[2]), .CS1(in_1[1]), .A(A[1]), .B(B[1]), .CS0(in_1[0]), .\output (out_6[1]),
    .Cout(n1_bit_alu_2_cout), .Cin(n1_bit_alu_1_cout));
  _1_Bit_ALU u_1_bit_alu_3 (
    .CS2(in_1[2]), .CS1(in_1[1]), .A(A[2]), .B(B[2]), .CS0(in_1[0]), .\output (out_6[2]),
    .Cout(n1_bit_alu_3_cout), .Cin(n1_bit_alu_2_cout));
  _1_Bit_ALU u_1_bit_alu_4 (
    .CS2(in_1[2]), .CS1(in_1[1]), .A(A[3]), .B(B[3]), .CS0(in_1[0]), .\output (out_6[3]), .Cout(CARRY),
    .Cin(n1_bit_alu_3_cout));
  nor nor_1 (ZERO, out_6[3], out_6[2], out_6[1], out_6[0]);
  xor xor_1 (OVERFLOW, n1_bit_alu_3_cout, CARRY);

  assign SIGN = out_6[3];
endmodule
