// Logisim project main.circ as structural Verilog: 10 circuits, main circuit main
module main (
  input  [15:0] _1st_Number,
  input  [15:0] _2nd_Number,
  output [15:0] Sum,
  output Overflow,
  output Underflow
);

  Floating_Point_Adder Floating_Point_Adder (
    .Overflow(Overflow), .Underflow(Underflow), .Sum(Sum), ._1st_Number(_1st_Number),
    ._2nd_Number(_2nd_Number));
endmodule

module Compare (
  input  [15:0] _1ST_SIGNIFICAND,
  input  [3:0] _1ST_EXPONENT,
  input  [15:0] _2ND_SIGNIFICAND,
  input  [3:0] _2ND_EXPONENT,
  output [3:0] OBTAINED_EXPONENT,
  output [14:0] SMALLER_SIGNIFICAND,
  output LARGER_SIGN,
  output [15:0] LARGER_SIGNIFICAND
);

  wire subtractor_1_bout, subtractor_2_bout;
  wire [3:0] multiplexer_1_out, negator_1_out, subtractor_1_out;
  wire [14:0] multiplexer_4_out;
  wire [15:0] multiplexer_3_out;

  Subtractor #(.width(4)) subtractor_1 (
    .a(_1ST_EXPONENT), .b(_2ND_EXPONENT), .out(subtractor_1_out), .bin(1'b0), .bout(subtractor_1_bout));
  Negator #(.width(4)) negator_1 (.in(subtractor_1_out), .out(negator_1_out));
  Subtractor #(.width(16)) subtractor_2 (
    .a({_1ST_EXPONENT, _1ST_SIGNIFICAND[14:3]}), .b({_2ND_EXPONENT, _2ND_SIGNIFICAND[14:3]}),
    .bout(subtractor_2_bout));  // open: out, bin
  Multiplexer #(.width(4), .enable("false")) multiplexer_1 (
    .in0(subtractor_1_out), .in1(negator_1_out), .out(multiplexer_1_out), .sel(subtractor_1_bout));
  Multiplexer #(.width(4), .enable("false")) multiplexer_2 (
    .in0(_1ST_EXPONENT), .in1(_2ND_EXPONENT), .out(OBTAINED_EXPONENT), .sel(subtractor_1_bout));
  Multiplexer #(.width(16), .enable("false")) multiplexer_3 (
    .in0(_2ND_SIGNIFICAND), .in1(_1ST_SIGNIFICAND), .out(multiplexer_3_out), .sel(subtractor_2_bout));
  Multiplexer #(.width(16), .enable("false")) multiplexer_4 (
    .in0(_1ST_SIGNIFICAND), .in1(_2ND_SIGNIFICAND), .out({LARGER_SIGN, multiplexer_4_out}),
    .sel(subtractor_2_bout));
  assign LARGER_SIGNIFICAND = {{1{1'b0}}, multiplexer_4_out};  // Bit_Extender bit_extender_1
  Shifter #(.width(15), .shift("lr")) shifter_1 (
    .in(multiplexer_3_out[14:0]), .\dist (multiplexer_1_out), .out(SMALLER_SIGNIFICAND));
endmodule

module Significand (
  input  [10:0] FRACTION,
  input  SIGN,
  output [15:0] SIGNIFICAND
);


  assign SIGNIFICAND = {SIGN, 1'b1, FRACTION, 3'b000};
endmodule

module Inverter (
  input  [14:0] SIGNIFICAND,
  input  SIGN,
  output [15:0] INVERTED_SIGNIFICAND
);

  wire [15:0] bit_extender_1_out, negator_1_out;

  assign bit_extender_1_out = {{1{1'b0}}, SIGNIFICAND};  // Bit_Extender bit_extender_1
  Negator #(.width(16)) negator_1 (.in(bit_extender_1_out), .out(negator_1_out));
  Multiplexer #(.width(16), .enable("false")) multiplexer_1 (
    .in0(bit_extender_1_out), .in1(negator_1_out), .out(INVERTED_SIGNIFICAND), .sel(SIGN));
endmodule

module Sign_check (
  input  _1ST_SIGN,
  input  _2ND_SIGN,
  output SIGN_SIMILARITY
);

  xor xor_1 (SIGN_SIMILARITY, _1ST_SIGN, _2ND_SIGN);
endmodule

module Adder (
  input  [15:0] _1st_Input,
  input  [15:0] _2nd_Input,
  output [15:0] Output
);

  Adder_part #(.width(16)) adder_1 (.a(_1st_Input), .b(_2nd_Input), .out(Output), .cin(1'b0));  // open: cout
endmodule

module Floating_Point_Adder (
  input  [15:0] _1st_Number,
  input  [15:0] _2nd_Number,
  output Overflow,
  output Underflow,
  output [15:0] Sum
);

  wire Compare_larger_sign, Sign_Check_sign_similarity;
  wire [3:0] Compare_obtained_exponent, Normalizer_exponent_out;
  wire [14:0] Compare_smaller_significand;
  wire [15:0] Adder_output, Compare_larger_significand, Inverter_inverted_significand,
       Normalizer_significand_out, Significand_2_significand, Significand_significand;

  Sign_check Sign_Check (
    ._1ST_SIGN(_1st_Number[15]), ._2ND_SIGN(_2nd_Number[15]), .SIGN_SIMILARITY(Sign_Check_sign_similarity));
  Significand Significand (.FRACTION(_1st_Number[10:0]), .SIGN(_1st_Number[15]), .SIGNIFICAND(Significand_significand));
  Adder Adder (
    ._1st_Input(Inverter_inverted_significand), ._2nd_Input(Compare_larger_significand), .Output(Adder_output));
  Truncation Truncation (
    .Significand(Normalizer_significand_out), .Exponent(Normalizer_exponent_out), .Sign(Compare_larger_sign),
    .Output(Sum));
  Compare Compare (
    ._1ST_SIGNIFICAND(Significand_significand), ._1ST_EXPONENT(_1st_Number[14:11]),
    ._2ND_SIGNIFICAND(Significand_2_significand), ._2ND_EXPONENT(_2nd_Number[14:11]),
    .OBTAINED_EXPONENT(Compare_obtained_exponent), .SMALLER_SIGNIFICAND(Compare_smaller_significand),
    .LARGER_SIGN(Compare_larger_sign), .LARGER_SIGNIFICAND(Compare_larger_significand));
  Inverter Inverter (
    .SIGNIFICAND(Compare_smaller_significand), .SIGN(Sign_Check_sign_similarity),
    .INVERTED_SIGNIFICAND(Inverter_inverted_significand));
  Normalizer Normalizer (
    .Exponent_In(Compare_obtained_exponent), .Significand_out(Normalizer_significand_out),
    .Overflow(Overflow), .Underflow(Underflow), .Significand_in(Adder_output),
    .Exponent_Out(Normalizer_exponent_out));
  Significand Significand_2 (
    .FRACTION(_2nd_Number[10:0]), .SIGN(_2nd_Number[15]), .SIGNIFICAND(Significand_2_significand));
endmodule

module Normalizer (
  input  [15:0] Significand_in,
  input  [3:0] Exponent_In,
  output [15:0] Significand_out,
  output [3:0] Exponent_Out,
  output Overflow,
  output Underflow
);

  wire not_1_out, or_1_out, subtractor_1_bout;
  wire [3:0] adder_1_out, bitfinder_1_index, multiplexer_1_out, subtractor_1_out, subtractor_2_out;
  wire [15:0] shifter_1_out, shifter_2_out;

  Shifter #(.width(16), .shift("lr")) shifter_1 (.in(Significand_in), .\dist (4'b0001), .out(shifter_1_out));
  or or_1 (or_1_out, Exponent_In[0], Exponent_In[1], Exponent_In[2], Exponent_In[3]);
  not not_1 (not_1_out, or_1_out);
  BitFinder #(.width(16), .\type ("high1")) bitfinder_1 (
    .in(Significand_in), .index(bitfinder_1_index));  // open: found
  Subtractor #(.width(4)) subtractor_1 (
    .a(Exponent_In), .b(subtractor_2_out), .out(subtractor_1_out), .bout(subtractor_1_bout));  // open: bin
  Adder_part #(.width(4)) adder_1 (.a(Exponent_In), .b(4'b0001), .out(adder_1_out));  // open: cin, cout
  Subtractor #(.width(4)) subtractor_2 (
    .a(4'b1110), .b(bitfinder_1_index), .out(subtractor_2_out), .bin(1'b0));  // open: bout
  Underflow underflow_1 (
    .Borrow_out(subtractor_1_bout), .Underflow(Underflow), .Exp_In(multiplexer_1_out),
    .in_2(Significand_in[15:14]));
  Shifter #(.width(16)) shifter_2 (.in(Significand_in), .\dist (subtractor_2_out), .out(shifter_2_out));
  Multiplexer #(.select(2), .width(4), .enable("false")) multiplexer_1 (
    .in0(subtractor_1_out), .in1(Exponent_In), .in2(adder_1_out), .in3(adder_1_out), .out(multiplexer_1_out),
    .sel(Significand_in[15:14]));
  Multiplexer #(.width(4), .enable("false")) multiplexer_2 (
    .in0(multiplexer_1_out), .in1(4'b0000), .out(Exponent_Out), .sel(not_1_out));
  and and_1 (Overflow, multiplexer_1_out[0], multiplexer_1_out[1], Significand_in[15], multiplexer_1_out[2], multiplexer_1_out[3]);
  Multiplexer #(.select(2), .width(16), .enable("false")) multiplexer_3 (
    .in0(shifter_2_out), .in1(Significand_in), .in2(shifter_1_out), .in3(shifter_1_out),
    .out(Significand_out), .sel(Significand_in[15:14]));
endmodule

module Underflow (
  input  [3:0] Exp_In,
  input  [1:0] in_2,
  input  Borrow_out,
  output Underflow
);

  wire and_1_out, not_1_out, not_2_out, or_1_out, or_2_out;

  not not_1 (not_1_out, or_1_out);
  or or_1 (or_1_out, in_2[0], in_2[1]);
  and and_1 (and_1_out, not_1_out, Borrow_out);
  or or_2 (or_2_out, Exp_In[0], Exp_In[1], Exp_In[2], Exp_In[3]);
  not not_2 (not_2_out, or_2_out);
  or or_3 (Underflow, not_2_out, and_1_out);
endmodule

module Truncation (
  input  [15:0] Significand,
  input  [3:0] Exponent,
  input  Sign,
  output [15:0] Output
);


  assign Output = {Sign, Exponent, Significand[13:3]};
endmodule
