// Logisim project Register.circ as structural Verilog: 1 circuit, main circuit Register Block
module Register_Block (
  input  [3:0] Read_1_Address,
  input  [7:0] Write_Data,
  input  RegWrite,
  input  Clk,
  input  [3:0] Write_Address,
  input  [3:0] Read_2_Address,
  output [7:0] Read_1_Data,
  output [7:0] Read_2_Data
);

  wire and_1_out, demultiplexer_1_out0, demultiplexer_1_out1, demultiplexer_1_out2, demultiplexer_1_out3,
       demultiplexer_1_out4, demultiplexer_1_out5, demultiplexer_1_out6;
  wire [7:0] sp_q, t0_q, t1_q, t2_q, t3_q, t4_q, t5_q, zero_q;

  and and_1 (and_1_out, RegWrite, Clk);
  Demultiplexer #(.select(3), .enable("false")) demultiplexer_1 (
    .out0(demultiplexer_1_out0), .out1(demultiplexer_1_out1), .out2(demultiplexer_1_out2),
    .out3(demultiplexer_1_out3), .out4(demultiplexer_1_out4), .out5(demultiplexer_1_out5),
    .out6(demultiplexer_1_out6), .in(and_1_out), .sel(Write_Address[2:0]));  // open: out7
  Register zero (.D({8{1'b0}}), .Q(zero_q), .clk(1'b0));  // open: en, clr
  Register t0 (.D(Write_Data), .Q(t0_q), .clk(demultiplexer_1_out0));  // open: en, clr
  Register t1 (.D(Write_Data), .Q(t1_q), .clk(demultiplexer_1_out1));  // open: en, clr
  Register t2 (.D(Write_Data), .Q(t2_q), .clk(demultiplexer_1_out2));  // open: en, clr
  Register t3 (.D(Write_Data), .Q(t3_q), .clk(demultiplexer_1_out3));  // open: en, clr
  Register t4 (.D(Write_Data), .Q(t4_q), .clk(demultiplexer_1_out4));  // open: en, clr
  Register t5 (.D(Write_Data), .Q(t5_q), .clk(demultiplexer_1_out5));  // open: en, clr
  Register sp (.D(Write_Data), .Q(sp_q), .clk(demultiplexer_1_out6));  // open: en, clr
  Multiplexer #(.select(3), .width(8), .disabled(0), .enable("false")) multiplexer_1 (
    .in0(t0_q), .in1(t1_q), .in2(t2_q), .in3(t3_q), .in4(t4_q), .in5(t5_q), .in6(sp_q), .in7(zero_q),
    .out(Read_1_Data), .sel(Read_1_Address[2:0]));
  Multiplexer #(.select(3), .width(8), .disabled(0), .enable("false")) multiplexer_2 (
    .in0(t0_q), .in1(t1_q), .in2(t2_q), .in3(t3_q), .in4(t4_q), .in5(t5_q), .in6(sp_q), .in7(zero_q),
    .out(Read_2_Data), .sel(Read_2_Address[2:0]));
endmodule
