// Logisim project alooo.circ as structural Verilog: 8 circuits, main circuit main
module main (
  input  [7:0] input_1,
  input  [2:0] AlUOp,
  input  [7:0] input_2,
  output Overflow,
  output Zero,
  output [7:0] \output 
);

  wire add_1_overflow, sub_1_overflow;
  wire [7:0] add_1_out_3, and_1_result, nor_1_result, or_1_result, sll_1_result, srl_1_result, sub_1_result;

  add add_1 (.X(input_1), .Y(input_2), .out_3(add_1_out_3), .overflow(add_1_overflow));
  sub sub_1 (.X(input_1), .Y(input_2), .Zero(Zero), .result(sub_1_result), .overflow(sub_1_overflow));
  \or  or_1 (.X(input_1), .Y(input_2), .result(or_1_result));
  \and  and_1 (.X(input_1), .Y(input_2), .result(and_1_result));
  \nor  nor_1 (.X(input_1), .Y(input_2), .result(nor_1_result));
  sll sll_1 (.X(input_2), .Y(input_1), .result(sll_1_result));
  srl srl_1 (.X(input_2), .Y(input_1), .result(srl_1_result));
  Multiplexer #(.select(3), .enable("false")) multiplexer_1 (
    .in0(add_1_overflow), .in1(sub_1_overflow), .in2(1'b0), .in3(1'b0), .in4(1'b0), .in5(1'b0), .in6(1'b0),
    .in7(1'b0), .out(Overflow), .sel(AlUOp));
  Multiplexer #(.select(3), .width(8), .enable("false")) multiplexer_2 (
    .in0(add_1_out_3), .in1(sub_1_result), .in2(or_1_result), .in3(and_1_result), .in4(nor_1_result),
    .in5(sll_1_result), .in6(srl_1_result), .out(\output ), .sel(AlUOp));  // open: in7
endmodule

module add (
  input  [7:0] X,
  input  [7:0] Y,
  output [7:0] out_3,
  output overflow
);

  wire adder_1_cout, adder_2_cout;

  Adder #(.width(7)) adder_1 (.a(X[6:0]), .b(Y[6:0]), .out(out_3[6:0]), .cout(adder_1_cout));  // open: cin
  Adder #(.width(1)) adder_2 (.a(X[7]), .b(Y[7]), .out(out_3[7]), .cin(adder_1_cout), .cout(adder_2_cout));
  xor xor_1 (overflow, adder_1_cout, adder_2_cout);
endmodule

module sub (
  input  [7:0] X,
  input  [7:0] Y,
  output Zero,
  output [7:0] result,
  output overflow
);

  wire or_1_out;
  wire [7:0] negator_1_out;

  Negator negator_1 (.in(Y), .out(negator_1_out));
  add add_1 (.X(X), .Y(negator_1_out), .out_3(result), .overflow(overflow));
  or or_1 (or_1_out, result[0], result[1], result[2], result[3], result[4], result[5], result[6], result[7]);
  not not_1 (Zero, or_1_out);
endmodule

module \and  (
  input  [7:0] X,
  input  [7:0] Y,
  output [7:0] result
);

  assign result = X & Y;  // AND_Gate and_1, 8 bits wide
endmodule

module \or  (
  input  [7:0] X,
  input  [7:0] Y,
  output [7:0] result
);

  assign result = X | Y;  // OR_Gate or_1, 8 bits wide
endmodule

module \nor  (
  input  [7:0] X,
  input  [7:0] Y,
  output [7:0] result
);

  wire [7:0] or_1_out;

  assign result = ~or_1_out;  // NOT_Gate not_1, 8 bits wide
  assign or_1_out = X | Y;  // OR_Gate or_1, 8 bits wide
endmodule

module sll (
  input  [7:0] X,
  input  [7:0] Y,
  output [7:0] result
);

  Shifter shifter_1 (.in(X), .\dist (Y[2:0]), .out(result));
endmodule

module srl (
  input  [7:0] X,
  input  [7:0] Y,
  output [7:0] result
);

  Shifter #(.shift("lr")) shifter_1 (.in(X), .\dist (Y[2:0]), .out(result));
endmodule
