// Logisim project Control.circ as structural Verilog: 1 circuit, main circuit Control_Part
module Control_Part (
  input  [3:0] OP_CODE,
  output RegWrite,
  output ALU_Src,
  output MemWrite,
  output [2:0] ALU_op,
  output MemToReg,
  output MemRead,
  output Bneq,
  output Beq,
  output Jump,
  output RegDst
);

  ROM #(.addrWidth(4), .dataWidth(12)) rom_1 (
    .addr(OP_CODE), .data({RegDst, Jump, Beq, Bneq, MemRead, MemToReg, ALU_op, MemWrite, ALU_Src, RegWrite}));  // open: sel
  // Probe on {RegDst, Jump, Beq, Bneq, MemRead, MemToReg, ALU_op, MemWrite, ALU_Src, RegWrite}

  // Notes on the sheet:
  //   contents of rom_1 (hex, n*v repeats v):
  //   821 801 811 3 3 829 400 1b b 831 3 b 809 13 819 b
endmodule
