// Logisim project Data Memory.circ as structural Verilog: 1 circuit, main circuit Data Memory
module Data_Memory (
  input  [7:0] Address,
  input  [7:0] Write_Data,
  input  MemRead,
  input  MemWrite,
  input  Clk,
  output [7:0] Output_Data
);

  RAM #(.bus("separate")) ram_1 (
    .addr(Address), .din(Write_Data), .data(Output_Data), .str(MemWrite), .clk(Clk), .ld(MemRead));  // open: sel, clr
endmodule
