// Logisim project Instruction Memory.circ as structural Verilog: 1 circuit, main circuit Instruction Block
module Instruction_Block (
  input  [7:0] Read_Address,
  output [19:0] Instruction
);

  ROM #(.dataWidth(20)) rom_1 (.addr(Read_Address), .data(Instruction));  // open: sel
endmodule
