// Logisim project MIPS.circ as structural Verilog: 11 circuits, main circuit MIPS
module MIPS (
);

  wire clock_1_out, not_1_out, not_2_out, not_3_out, not_4_out;
  wire [1:0] forwarding_circuit_1_forward_a, forwarding_circuit_1_forward_b;
  wire [3:0] ex_mem_block_1_rd_2, id_ex_block_1_rd_output, id_ex_block_1_rs_output, id_ex_block_1_rt_output,
       mem_wb_block_1_rd_2;
  wire [7:0] adder_1_out, data_memory_1_output_data, ex_mem_block_1_data_1_output,
       ex_mem_block_1_data_2_output, id_ex_block_1_read_1_output, id_ex_block_1_read_2_output, main_1_output,
       mem_wb_block_1_data_1_output, mem_wb_block_1_data_2_output, multiplexer_1_out, multiplexer_2_out,
       multiplexer_3_out, register_1_q, register_2_read_1_data, register_2_read_2_data, register_2_t0,
       register_2_t1, register_2_t2, register_2_t3, register_2_t4;
  wire [11:0] control_1_all, ex_mem_block_1_control_2, id_ex_block_1_control_output, mem_wb_block_1_control_2;
  wire [19:0] if_id_block_1_ins_output, instruction_1_instruction;

  Clock clock_1 (.out(clock_1_out));
  // Probe on register_2_t4
  // Probe on register_2_t3
  // Probe on register_2_t2
  // Probe on register_2_t1
  // Probe on register_2_t0
  // Probe on adder_1_out
  Register_part #(.trigger("falling")) register_1 (
    .D(adder_1_out), .Q(register_1_q), .clk(clock_1_out));  // open: en, clr
  Adder adder_1 (.a(register_1_q), .b(8'h1), .out(adder_1_out));  // open: cin, cout
  // Probe on instruction_1_instruction
  Instruction instruction_1 (.Read_Address(register_1_q), .Instruction(instruction_1_instruction));
  not not_1 (not_1_out, clock_1_out);
  IF_ID_Block if_id_block_1 (
    .instruction(instruction_1_instruction), .CLK(not_1_out), .Ins_output(if_id_block_1_ins_output));
  // Probe on if_id_block_1_ins_output[19:16]
  // Probe on control_1_all
  // Probe on if_id_block_1_ins_output[15:12]
  // Probe on if_id_block_1_ins_output[11:8]
  Control control_1 (
    .OP_CODE(if_id_block_1_ins_output[19:16]), .ALL(control_1_all));  // open: RegWrite, ALU_Src, MemWrite, ALU_op, MemToReg, MemRead, Bneq, Beq, Jump, RegDst
  Register register_2 (
    .Read_1_Address(if_id_block_1_ins_output[15:12]), .Write_Data(multiplexer_3_out),
    .RegWrite(mem_wb_block_1_control_2[0]), .Clk(clock_1_out), .Write_Address(mem_wb_block_1_rd_2),
    .Read_2_Address(if_id_block_1_ins_output[11:8]), .Read_1_Data(register_2_read_1_data),
    .Read_2_Data(register_2_read_2_data), .t0(register_2_t0), .t1(register_2_t1), .t2(register_2_t2),
    .t3(register_2_t3), .t4(register_2_t4));  // open: t5, sp
  ID_EX_Block id_ex_block_1 (
    .Control(control_1_all), .Read_Data_1(register_2_read_1_data), .Read_Data_2(register_2_read_2_data),
    .rs(if_id_block_1_ins_output[15:12]), .rt(if_id_block_1_ins_output[11:8]),
    .rd(if_id_block_1_ins_output[7:4]), .Control_Output(id_ex_block_1_control_output),
    .Read_1_output(id_ex_block_1_read_1_output), .Read_2_output(id_ex_block_1_read_2_output),
    .rs_output(id_ex_block_1_rs_output), .rt_output(id_ex_block_1_rt_output),
    .rd_output(id_ex_block_1_rd_output), .CLK(not_2_out));
  // Probe on register_2_read_1_data
  // Probe on register_2_read_2_data
  not not_2 (not_2_out, clock_1_out);
  // Probe on id_ex_block_1_control_output
  // Probe on id_ex_block_1_read_1_output
  // Probe on id_ex_block_1_read_2_output
  // Probe on forwarding_circuit_1_forward_a
  Forwarding_Circuit forwarding_circuit_1 (
    .Forward_A(forwarding_circuit_1_forward_a), .Forward_B(forwarding_circuit_1_forward_b),
    .ID_EX_rs(id_ex_block_1_rs_output), .ID_EX_rt(id_ex_block_1_rt_output), .EX_MEM_rd(ex_mem_block_1_rd_2),
    .EX_MEM_RegWrite(ex_mem_block_1_control_2[0]), .MEM_WB_rd(mem_wb_block_1_rd_2),
    .MEM_WB_RegWrite(mem_wb_block_1_control_2[0]));
  // Probe on forwarding_circuit_1_forward_b
  // Probe on id_ex_block_1_control_output[5:3]
  Multiplexer #(.select(2), .width(8), .enable("false")) multiplexer_1 (
    .in0(id_ex_block_1_read_1_output), .in1(multiplexer_3_out), .in2(ex_mem_block_1_data_1_output),
    .out(multiplexer_1_out), .sel(forwarding_circuit_1_forward_a));  // open: in3
  // Probe on multiplexer_1_out
  Multiplexer #(.select(2), .width(8), .enable("false")) multiplexer_2 (
    .in0(id_ex_block_1_read_2_output), .in1(multiplexer_3_out), .in2(ex_mem_block_1_data_1_output),
    .out(multiplexer_2_out), .sel(forwarding_circuit_1_forward_b));  // open: in3
  alooo_main main_1 (
    .input_1(multiplexer_1_out), .AlUOp(id_ex_block_1_control_output[5:3]), .input_2(multiplexer_2_out),
    .\output (main_1_output));  // open: Overflow, Zero
  // Probe on multiplexer_2_out
  // Probe on main_1_output
  EX_MEM_Block ex_mem_block_1 (
    .control(id_ex_block_1_control_output), .Data_1(main_1_output), .Data_2(id_ex_block_1_read_2_output),
    .rd(id_ex_block_1_rd_output), .clock(not_3_out), .control_2(ex_mem_block_1_control_2),
    .Data_1_output(ex_mem_block_1_data_1_output), .Data_2_output(ex_mem_block_1_data_2_output),
    .rd_2(ex_mem_block_1_rd_2));
  not not_3 (not_3_out, clock_1_out);
  // Probe on ex_mem_block_1_control_2
  Data_Memory data_memory_1 (
    .Address(ex_mem_block_1_data_1_output), .Write_Data(ex_mem_block_1_data_2_output),
    .Output_Data(data_memory_1_output_data), .MemWrite(ex_mem_block_1_control_2[2]), .Clk(clock_1_out),
    .MemRead(ex_mem_block_1_control_2[7]));
  // Probe on ex_mem_block_1_data_1_output
  MEM_WB_Block mem_wb_block_1 (
    .control(ex_mem_block_1_control_2), .control_2(mem_wb_block_1_control_2),
    .Data_1(ex_mem_block_1_data_1_output), .Data_1_output(mem_wb_block_1_data_1_output),
    .Data_2(data_memory_1_output_data), .Data_2_output(mem_wb_block_1_data_2_output),
    .rd(ex_mem_block_1_rd_2), .rd_2(mem_wb_block_1_rd_2), .clock(not_4_out));
  not not_4 (not_4_out, clock_1_out);
  // Probe on multiplexer_3_out
  Multiplexer #(.width(8), .enable("false")) multiplexer_3 (
    .in0(mem_wb_block_1_data_1_output), .in1(mem_wb_block_1_data_2_output), .out(multiplexer_3_out),
    .sel(mem_wb_block_1_control_2[6]));
endmodule

module Instruction (
  input  [7:0] Read_Address,
  output [19:0] Instruction
);

  ROM #(.dataWidth(20)) rom_1 (.addr(Read_Address), .data(Instruction));  // open: sel

  // Notes on the sheet:
  //   contents of rom_1 (hex, n*v repeats v):
  //   12310 c2340 23140 14340
endmodule

module Data_Memory (
  input  [7:0] Address,
  input  [7:0] Write_Data,
  input  MemRead,
  input  MemWrite,
  input  Clk,
  output [7:0] Output_Data
);

  RAM #(.bus("separate")) ram_1 (
    .addr(Address), .din(Write_Data), .data(Output_Data), .str(MemWrite), .clk(Clk), .ld(MemRead));  // open: sel, clr
endmodule

module Register (
  input  [3:0] Read_1_Address,
  input  [7:0] Write_Data,
  input  RegWrite,
  input  Clk,
  input  [3:0] Write_Address,
  input  [3:0] Read_2_Address,
  output [7:0] Read_1_Data,
  output [7:0] Read_2_Data,
  output [7:0] t0,
  output [7:0] t1,
  output [7:0] t2,
  output [7:0] t3,
  output [7:0] t4,
  output [7:0] t5,
  output [7:0] sp
);

  wire and_1_out, demultiplexer_1_out0, demultiplexer_1_out1, demultiplexer_1_out2, demultiplexer_1_out3,
       demultiplexer_1_out4, demultiplexer_1_out5, demultiplexer_1_out6;
  wire [7:0] zero_q;

  and and_1 (and_1_out, RegWrite, Clk);
  Demultiplexer #(.select(3), .enable("false")) demultiplexer_1 (
    .out0(demultiplexer_1_out0), .out1(demultiplexer_1_out1), .out2(demultiplexer_1_out2),
    .out3(demultiplexer_1_out3), .out4(demultiplexer_1_out4), .out5(demultiplexer_1_out5),
    .out6(demultiplexer_1_out6), .in(and_1_out), .sel(Write_Address[2:0]));  // open: out7
  Register_part zero (.D({8{1'b0}}), .Q(zero_q), .clk(1'b0));  // open: en, clr
  Register_part u_t0 (.D(Write_Data), .Q(t0), .clk(demultiplexer_1_out0));  // open: en, clr
  Register_part u_t1 (.D(Write_Data), .Q(t1), .clk(demultiplexer_1_out1));  // open: en, clr
  Register_part u_t2 (.D(Write_Data), .Q(t2), .clk(demultiplexer_1_out2));  // open: en, clr
  Register_part u_t3 (.D(Write_Data), .Q(t3), .clk(demultiplexer_1_out3));  // open: en, clr
  Register_part u_t4 (.D(Write_Data), .Q(t4), .clk(demultiplexer_1_out4));  // open: en, clr
  Register_part u_t5 (.D(Write_Data), .Q(t5), .clk(demultiplexer_1_out5));  // open: en, clr
  Register_part u_sp (.D(Write_Data), .Q(sp), .clk(demultiplexer_1_out6));  // open: en, clr
  Multiplexer #(.select(3), .width(8), .disabled(0), .enable("false")) multiplexer_1 (
    .in0(t0), .in1(t1), .in2(t2), .in3(t3), .in4(t4), .in5(t5), .in6(sp), .in7(zero_q), .out(Read_1_Data),
    .sel(Read_1_Address[2:0]));
  Multiplexer #(.select(3), .width(8), .disabled(0), .enable("false")) multiplexer_2 (
    .in0(t0), .in1(t1), .in2(t2), .in3(t3), .in4(t4), .in5(t5), .in6(sp), .in7(zero_q), .out(Read_2_Data),
    .sel(Read_2_Address[2:0]));
endmodule

module Control (
  input  [3:0] OP_CODE,
  output RegWrite,
  output ALU_Src,
  output MemWrite,
  output [2:0] ALU_op,
  output MemToReg,
  output MemRead,
  output Bneq,
  output Beq,
  output Jump,
  output RegDst,
  output [11:0] ALL
);

  ROM #(.addrWidth(4), .dataWidth(12)) rom_1 (.addr(OP_CODE), .data(ALL));  // open: sel

  assign ALU_op = ALL[5:3];
  assign ALU_Src = ALL[1];
  assign Beq = ALL[9];
  assign Bneq = ALL[8];
  assign Jump = ALL[10];
  assign MemRead = ALL[7];
  assign MemToReg = ALL[6];
  assign MemWrite = ALL[2];
  assign RegDst = ALL[11];
  assign RegWrite = ALL[0];

  // Notes on the sheet:
  //   contents of rom_1 (hex, n*v repeats v):
  //   0 801 811 3 6 829 400 1b 208 831 c3 b 809 13 819 108
endmodule

module Shift_Logical_unit (
  input  [3:0] Op_code,
  output Value
);

  wire and_1_out, and_2_out, not_1_out, not_2_out, not_3_out, not_4_out;

  not not_1 (not_1_out, Op_code[1]);
  not not_2 (not_2_out, Op_code[3]);
  not not_3 (not_3_out, Op_code[1]);
  not not_4 (not_4_out, Op_code[2]);
  and and_1 (and_1_out, Op_code[0], not_1_out, Op_code[2], not_2_out);
  and and_2 (and_2_out, Op_code[0], not_3_out, not_4_out, Op_code[3]);
  or or_1 (Value, and_1_out, and_2_out);
endmodule

module IF_ID_Block (
  input  [19:0] instruction,
  input  CLK,
  output [19:0] Ins_output
);

  Register_part #(.width(20)) register_1 (.D(instruction), .Q(Ins_output), .clk(CLK));  // open: en, clr
endmodule

module MEM_WB_Block (
  input  [11:0] control,
  input  [7:0] Data_1,
  input  [7:0] Data_2,
  input  [3:0] rd,
  input  clock,
  output [11:0] control_2,
  output [7:0] Data_1_output,
  output [7:0] Data_2_output,
  output [3:0] rd_2
);

  Register_part #(.width(12)) register_1 (.D(control), .Q(control_2), .clk(clock));  // open: en, clr
  Register_part register_2 (.D(Data_1), .Q(Data_1_output), .clk(clock));  // open: en, clr
  Register_part register_3 (.D(Data_2), .Q(Data_2_output), .clk(clock));  // open: en, clr
  Register_part #(.width(4)) register_4 (.D(rd), .Q(rd_2), .clk(clock));  // open: en, clr
endmodule

module ID_EX_Block (
  input  [11:0] Control,
  input  [7:0] Read_Data_1,
  input  [7:0] Read_Data_2,
  input  [3:0] rs,
  input  [3:0] rt,
  input  [3:0] rd,
  input  CLK,
  output [11:0] Control_Output,
  output [7:0] Read_1_output,
  output [7:0] Read_2_output,
  output [3:0] rs_output,
  output [3:0] rt_output,
  output [3:0] rd_output
);

  // Probe on Control
  Register_part #(.width(12)) register_1 (.D(Control), .Q(Control_Output), .clk(CLK));  // open: en, clr
  Register_part register_2 (.D(Read_Data_1), .Q(Read_1_output), .clk(CLK));  // open: en, clr
  Register_part register_3 (.D(Read_Data_2), .Q(Read_2_output), .clk(CLK));  // open: en, clr
  Register_part #(.width(4)) register_4 (.D(rs), .Q(rs_output), .clk(CLK));  // open: en, clr
  Register_part #(.width(4)) register_5 (.D(rt), .Q(rt_output), .clk(CLK));  // open: en, clr
  Register_part #(.width(4)) register_6 (.D(rd), .Q(rd_output), .clk(CLK));  // open: en, clr
endmodule

module EX_MEM_Block (
  input  [11:0] control,
  input  [7:0] Data_1,
  input  [7:0] Data_2,
  input  [3:0] rd,
  input  clock,
  output [11:0] control_2,
  output [7:0] Data_1_output,
  output [7:0] Data_2_output,
  output [3:0] rd_2
);

  Register_part #(.width(12)) register_1 (.D(control), .Q(control_2), .clk(clock));  // open: en, clr
  Register_part register_2 (.D(Data_1), .Q(Data_1_output), .clk(clock));  // open: en, clr
  Register_part register_3 (.D(Data_2), .Q(Data_2_output), .clk(clock));  // open: en, clr
  Register_part #(.width(4)) register_4 (.D(rd), .Q(rd_2), .clk(clock));  // open: en, clr
endmodule

module Forwarding_Circuit (
  input  [3:0] ID_EX_rs,
  input  [3:0] ID_EX_rt,
  input  [3:0] EX_MEM_rd,
  input  EX_MEM_RegWrite,
  input  [3:0] MEM_WB_rd,
  input  MEM_WB_RegWrite,
  output [1:0] Forward_A,
  output [1:0] Forward_B
);

  wire and_1_out, and_2_out, and_3_out, and_4_out, and_7_out, and_8_out, comparator_1_eq, comparator_2_eq,
       comparator_3_eq, comparator_4_eq, not_1_out, not_2_out, not_3_out, not_4_out, not_5_out, not_6_out;

  Comparator #(.width(4)) comparator_1 (.a(EX_MEM_rd), .b(ID_EX_rs), .eq(comparator_1_eq));  // open: gt, lt
  Comparator #(.width(4)) comparator_2 (.a(EX_MEM_rd), .b(ID_EX_rt), .eq(comparator_2_eq));  // open: gt, lt
  Comparator #(.width(4)) comparator_3 (.a(MEM_WB_rd), .b(ID_EX_rs), .eq(comparator_3_eq));  // open: gt, lt
  Comparator #(.width(4)) comparator_4 (.a(MEM_WB_rd), .b(ID_EX_rt), .eq(comparator_4_eq));  // open: gt, lt
  and and_1 (and_1_out, EX_MEM_rd[0], EX_MEM_rd[1], EX_MEM_rd[2]);
  and and_2 (and_2_out, EX_MEM_rd[0], EX_MEM_rd[1], EX_MEM_rd[2]);
  and and_3 (and_3_out, MEM_WB_rd[0], MEM_WB_rd[1], MEM_WB_rd[2]);
  and and_4 (and_4_out, MEM_WB_rd[0], MEM_WB_rd[1], MEM_WB_rd[2]);
  not not_1 (not_1_out, and_1_out);
  not not_2 (not_2_out, and_2_out);
  not not_3 (not_3_out, and_3_out);
  not not_4 (not_4_out, and_4_out);
  and and_5 (Forward_A[1], comparator_1_eq, not_1_out, EX_MEM_RegWrite);
  and and_6 (Forward_B[1], comparator_2_eq, not_2_out, EX_MEM_RegWrite);
  and and_7 (and_7_out, comparator_3_eq, not_3_out, MEM_WB_RegWrite);
  and and_8 (and_8_out, comparator_4_eq, not_4_out, MEM_WB_RegWrite);
  not not_5 (not_5_out, Forward_A[1]);
  not not_6 (not_6_out, Forward_B[1]);
  and and_9 (Forward_A[0], not_5_out, and_7_out);
  and and_10 (Forward_B[0], not_6_out, and_8_out);
endmodule
